// Logisim project control_logic.circ as structural Verilog: 1 circuit, main circuit control_logic
module control_logic (
  input  [31:0] inst,
  input  BrEq,
  input  BrLt,
  output PCSel,
  output RegWEn,
  output [2:0] ImmSel,
  output BrUn,
  output ASel,
  output BSel,
  output [3:0] ALUSel,
  output MemRW,
  output [1:0] WBSel
);

  wire and_1_out, and_2_out, and_3_out, and_4_out, Br0, comparator_1_eq, comparator_2_eq, comparator_3_eq,
       comparator_4_eq, comparator_5_eq, comparator_6_eq, comparator_7_eq, comparator_9_eq, comparator_10_eq,
       comparator_12_eq, comparator_15_eq, comparator_16_eq, comparator_17_eq, comparator_18_eq,
       comparator_19_eq, comparator_20_eq, comparator_21_eq, comparator_22_eq, comparator_23_eq,
       comparator_24_eq, comparator_27_eq, comparator_28_eq, comparator_30_eq, comparator_31_eq, not_1_out,
       not_2_out, or_6_out, or_7_out, or_8_out;
  wire [1:1] comparator_14_eq;
  wire [2:0] or_3_out;
  wire [3:0] ALUSel1, ALUSel2, Sel0, Sel1, Sel5, Sel7;
  wire [4:0] or_9_out;

  Comparator #(.width(7), .mode("unsigned")) comparator_1 (
    .a(7'b0010111), .b(inst[6:0]), .eq(comparator_1_eq));  // open: gt, lt
  Comparator #(.width(7), .mode("unsigned")) comparator_2 (
    .a(7'b1100011), .b(inst[6:0]), .eq(comparator_2_eq));  // open: gt, lt
  Comparator #(.width(7), .mode("unsigned")) comparator_3 (
    .a(7'b1100111), .b(inst[6:0]), .eq(comparator_3_eq));  // open: gt, lt
  Comparator #(.width(7), .mode("unsigned")) comparator_4 (
    .a(7'b1101111), .b(inst[6:0]), .eq(comparator_4_eq));  // open: gt, lt
  or or_1 (PCSel, Br0, comparator_3_eq, comparator_4_eq);
  Comparator #(.width(7)) comparator_5 (.a(inst[6:0]), .b(7'b0110011), .eq(comparator_5_eq));  // open: gt, lt
  Comparator #(.width(7)) comparator_6 (.a(inst[6:0]), .b(7'b0010111), .eq(comparator_6_eq));  // open: gt, lt
  Comparator #(.width(7)) comparator_7 (.a(inst[6:0]), .b(7'b0010011), .eq(comparator_7_eq));  // open: gt, lt
  Comparator #(.width(7)) comparator_8 (.a(inst[6:0]), .b(7'b0000011), .eq(or_3_out[1]));  // open: gt, lt
  Comparator #(.width(7)) comparator_9 (.a(inst[6:0]), .b(7'b1101111), .eq(comparator_9_eq));  // open: gt, lt
  Comparator #(.width(7)) comparator_10 (.a(inst[6:0]), .b(7'b1100111), .eq(comparator_10_eq));  // open: gt, lt
  Comparator #(.width(7), .mode("unsigned")) comparator_11 (.a(7'b0100011), .b(inst[6:0]), .eq(MemRW));  // open: gt, lt
  or or_2 (ASel, comparator_1_eq, comparator_2_eq, comparator_4_eq);
  Multiplexer #(.select(2), .width(4), .enable("false")) multiplexer_1 (
    .in0(4'b0000), .in1(4'b1010), .in2(4'b1100), .out(Sel0), .sel({inst[30], inst[25]}));  // open: in3
  or or_3 (or_3_out[0], comparator_5_eq, comparator_6_eq, comparator_7_eq);
  or or_4 (or_3_out[2], comparator_9_eq, comparator_10_eq);
  Comparator #(.width(7)) comparator_12 (.a(inst[6:0]), .b(7'b0110111), .eq(comparator_12_eq));  // open: gt, lt
  Multiplexer #(.select(3), .width(4), .enable("false")) multiplexer_2 (
    .in0(Sel0), .in1(Sel1), .in2(4'b0111), .in3(4'b1011), .in4(4'b0011), .in5(Sel5), .in6(4'b0010),
    .in7(Sel7), .out(ALUSel1), .sel(inst[14:12]));
  Multiplexer #(.select(2), .width(4), .enable("false")) multiplexer_3 (
    .in0(4'b0110), .in1(4'b1110), .out(Sel1), .sel({inst[30], inst[25]}));  // open: in2, in3
  Multiplexer #(.select(3), .width(2), .enable("false")) multiplexer_4 (
    .in0(2'b00), .in1(2'b01), .in2(2'b10), .in4(2'b11), .out(WBSel), .sel(or_3_out));  // open: in3, in5, in6, in7
  or or_5 (RegWEn, or_3_out[0], or_3_out[1], or_3_out[2], comparator_12_eq);
  Multiplexer #(.select(2), .width(4), .enable("false")) multiplexer_5 (
    .in0(4'b0100), .in1(4'b1000), .in2(4'b0101), .out(Sel5), .sel({inst[30], inst[25]}));  // open: in3
  Comparator #(.width(7)) comparator_13 (.a(inst[6:0]), .b(7'b0110011), .eq(BSel));  // open: gt, lt
  Comparator #(.width(7)) comparator_14 (.a(inst[6:0]), .b(7'b0010011), .eq(comparator_14_eq[1]));  // open: gt, lt
  Multiplexer #(.select(3), .width(4), .enable("false")) multiplexer_6 (
    .in0(4'b0000), .in1(4'b0110), .in2(4'b0111), .in3(4'b1011), .in4(4'b0011), .in5(Sel5), .in6(4'b0010),
    .in7(4'b0001), .out(ALUSel2), .sel(inst[14:12]));
  Multiplexer #(.select(2), .width(4), .enable("false")) multiplexer_7 (
    .in0(4'b0001), .in1(4'b1001), .out(Sel7), .sel({inst[30], inst[25]}));  // open: in2, in3
  Multiplexer #(.select(2), .width(4), .enable("false")) multiplexer_8 (
    .in0(4'b0000), .in1(ALUSel1), .in2(ALUSel2), .out(ALUSel), .sel({comparator_14_eq[1], BSel}));  // open: in3
  Comparator #(.width(7), .mode("unsigned")) comparator_15 (
    .a(7'b1100011), .b(inst[6:0]), .eq(comparator_15_eq));  // open: gt, lt
  Comparator #(.width(3), .mode("unsigned")) comparator_16 (
    .a(3'b000), .b(inst[14:12]), .eq(comparator_16_eq));  // open: gt, lt
  Comparator #(.width(3), .mode("unsigned")) comparator_17 (
    .a(3'b001), .b(inst[14:12]), .eq(comparator_17_eq));  // open: gt, lt
  not not_1 (not_1_out, BrEq);
  Comparator #(.width(3), .mode("unsigned")) comparator_18 (
    .a(3'b100), .b(inst[14:12]), .eq(comparator_18_eq));  // open: gt, lt
  Comparator #(.width(3), .mode("unsigned")) comparator_19 (
    .a(3'b110), .b(inst[14:12]), .eq(comparator_19_eq));  // open: gt, lt
  Comparator #(.width(3), .mode("unsigned")) comparator_20 (
    .a(3'b101), .b(inst[14:12]), .eq(comparator_20_eq));  // open: gt, lt
  Comparator #(.width(3), .mode("unsigned")) comparator_21 (
    .a(3'b111), .b(inst[14:12]), .eq(comparator_21_eq));  // open: gt, lt
  not not_2 (not_2_out, BrLt);
  and and_1 (and_1_out, comparator_16_eq, BrEq);
  and and_2 (and_2_out, comparator_17_eq, not_1_out);
  or or_6 (or_6_out, comparator_18_eq, comparator_19_eq);
  and and_3 (and_3_out, or_6_out, BrLt);
  or or_7 (or_7_out, comparator_20_eq, comparator_21_eq);
  and and_4 (and_4_out, or_7_out, not_2_out);
  Comparator #(.width(7)) comparator_22 (.a(inst[6:0]), .b(7'b0000011), .eq(comparator_22_eq));  // open: gt, lt
  Comparator #(.width(7)) comparator_23 (.a(inst[6:0]), .b(7'b0010011), .eq(comparator_23_eq));  // open: gt, lt
  Comparator #(.width(7)) comparator_24 (.a(inst[6:0]), .b(7'b1100111), .eq(comparator_24_eq));  // open: gt, lt
  Comparator #(.width(7)) comparator_25 (.a(inst[6:0]), .b(7'b0100011), .eq(or_9_out[1]));  // open: gt, lt
  Comparator #(.width(7)) comparator_26 (.a(inst[6:0]), .b(7'b1100011), .eq(or_9_out[2]));  // open: gt, lt
  Comparator #(.width(7)) comparator_27 (.a(inst[6:0]), .b(7'b0010111), .eq(comparator_27_eq));  // open: gt, lt
  Comparator #(.width(7)) comparator_28 (.a(inst[6:0]), .b(7'b0110111), .eq(comparator_28_eq));  // open: gt, lt
  Comparator #(.width(7)) comparator_29 (.a(inst[6:0]), .b(7'b1101111), .eq(or_9_out[4]));  // open: gt, lt
  or or_8 (or_8_out, and_1_out, and_2_out, and_3_out, and_4_out);
  or or_9 (or_9_out[0], comparator_22_eq, comparator_23_eq, comparator_24_eq);
  or or_10 (or_9_out[3], comparator_27_eq, comparator_28_eq);
  and and_5 (Br0, comparator_15_eq, or_8_out);
  Multiplexer #(.select(5), .width(3), .enable("false")) multiplexer_9 (
    .in1(3'b001), .in2(3'b010), .in4(3'b011), .in8(3'b100), .in16(3'b101), .out(ImmSel), .sel(or_9_out));  // open: in0, in3, in5, in6, in7, in9, in10, in11, in12, in13, in14, in15, in17, in18, in19, in20, in21, in22, in23, in24, in25, in26, in27, in28, in29, in30, in31
  Comparator #(.width(3)) comparator_30 (.a(3'b110), .b(inst[14:12]), .eq(comparator_30_eq));  // open: gt, lt
  Comparator #(.width(3)) comparator_31 (.a(inst[14:12]), .b(3'b111), .eq(comparator_31_eq));  // open: gt, lt
  or or_11 (BrUn, comparator_30_eq, comparator_31_eq);

  // Other names for the same wires on the sheet: Opcode[6:0] = inst[6:0]; Funct3[2:0] = inst[14:12];
  //   Funct7[6:0] = inst[31:25]; Sel[1:0] = {inst[30], inst[25]}

  // Notes on the sheet:
  //   INPUTS to your circuit
  //   DON'T CHANGE THE LOCATIONS OF THE INPUTS AND OUTPUTS!
  //   OUTPUT from your circuit
endmodule
