// Logisim project cpu.circ as structural Verilog: 1 circuit, main circuit main
module main (
  input  [31:0] INSTRUCTION,
  input  CLOCK,
  output [31:0] PROGRAM_COUNTER,
  output [31:0] ra,
  output [31:0] sp,
  output [31:0] t0,
  output [31:0] t1,
  output [31:0] t2,
  output [31:0] s0,
  output [31:0] s1,
  output [31:0] a0
);

  wire ASel, branch_comp_1_breq, branch_comp_1_brlt, control_logic_1_brun, control_logic_1_bsel,
       control_logic_1_memrw, PCSel, RegWEn;
  wire [1:0] control_logic_1_wbsel;
  wire [2:0] control_logic_1_immsel;
  wire [3:0] control_logic_1_alusel;
  wire [4:0] rd, rs1, rs2;
  wire [31:0] adder_1_out, adder_2_out, ALURes, Aout, Bout, DMEM_p5, imm, multiplexer_1_out,
       multiplexer_2_out, pc, register_1_q, rs1out, rs2out, wb;

  control_logic control_logic_1 (
    .BSel(control_logic_1_bsel), .ASel(ASel), .BrUn(control_logic_1_brun), .ImmSel(control_logic_1_immsel),
    .RegWEn(RegWEn), .PCSel(PCSel), .BrLt(branch_comp_1_brlt), .BrEq(branch_comp_1_breq),
    .inst({register_1_q[31:25], rs2, rs1, register_1_q[14:12], rd, register_1_q[6:0]}),
    .ALUSel(control_logic_1_alusel), .MemRW(control_logic_1_memrw), .WBSel(control_logic_1_wbsel));
  Register #(.width(32)) register_1 (
    .D(multiplexer_1_out), .clk(CLOCK),
    .Q({register_1_q[31:25], rs2, rs1, register_1_q[14:12], rd, register_1_q[6:0]}));  // open: en, clr
  Multiplexer #(.width(32), .enable("false")) multiplexer_1 (
    .in0(INSTRUCTION), .in1(32'h13), .out(multiplexer_1_out), .sel(PCSel));
  Adder #(.width(32)) adder_1 (.a(PROGRAM_COUNTER), .b(32'h4), .out(adder_1_out));  // open: cin, cout
  Multiplexer #(.width(32), .enable("false")) multiplexer_2 (
    .in0(adder_1_out), .in1(ALURes), .out(multiplexer_2_out), .sel(PCSel));
  Register #(.width(32)) u_PC (.D(multiplexer_2_out), .clk(CLOCK), .Q(PROGRAM_COUNTER));  // open: en, clr
  imm_gen imm_gen_1 (
    .ImmSel(control_logic_1_immsel),
    .inst({register_1_q[31:25], rs2, rs1, register_1_q[14:12], rd, register_1_q[6:0]}), .imm(imm));
  regfile_main RegFile (
    .rs2(rs2), .rd(rd), .Read_Data_1(rs1out), .Read_Data_2(rs2out), .ra(ra), .sp(sp), .t0(t0), .t1(t1),
    .t2(t2), .s0(s0), .s1(s1), .a0(a0), .rs1(rs1), .Write_Data(wb), .RegWEn(RegWEn), .clk(CLOCK));
  branch_comp branch_comp_1 (
    .BrEq(branch_comp_1_breq), .BrUn(control_logic_1_brun), .rs1(rs1out), .BrLt(branch_comp_1_brlt),
    .rs2(rs2out));
  Multiplexer #(.width(32), .enable("false")) multiplexer_3 (
    .in0(imm), .in1(rs2out), .out(Bout), .sel(control_logic_1_bsel));
  alu Arithmetic_Logic_Unit (.Result(ALURes), .ALUSel(control_logic_1_alusel), .A(Aout), .B(Bout));
  Register #(.width(32)) register_2 (.D(PROGRAM_COUNTER), .clk(CLOCK), .Q(pc));  // open: en, clr
  Multiplexer #(.width(32), .enable("false")) multiplexer_4 (.in0(rs1out), .in1(pc), .out(Aout), .sel(ASel));
  // mem_main DMEM: pin names not known; wires that end beside it: ALURes, rs2out, CLOCK, control_logic_1_memrw, DMEM_p5
  Multiplexer #(.select(2), .width(32), .enable("false")) multiplexer_5 (
    .in0(imm), .in1(ALURes), .in2(DMEM_p5), .in3(adder_2_out), .out(wb), .sel(control_logic_1_wbsel));
  Adder #(.width(32)) adder_2 (.a(pc), .b(32'h4), .out(adder_2_out));  // open: cin, cout

  // Other names for the same wires on the sheet: clk = CLOCK

  // Notes on the sheet:
  //   Output
  //   IMEM (do **NOT** move this)
  //   Inputs
  //   Inputs/Outputs for testing. Do **NOT** move these.
endmodule
