// Logisim project imm_gen.circ as structural Verilog: 1 circuit, main circuit imm_gen
module imm_gen (
  input  [31:0] inst,
  input  [2:0] ImmSel,
  output [31:0] imm
);

  wire [31:0] shifter_1_out, shifter_2_out, shifter_3_out, shifter_4_out;

  Shifter #(.width(32), .shift("ar")) shifter_1 (
    .in({inst[31:20], {20{1'b0}}}), .\dist (5'b10100), .out(shifter_1_out));
  Shifter #(.width(32), .shift("ar")) shifter_2 (
    .in({inst[31:25], inst[11:7], {20{1'b0}}}), .\dist (5'b10100), .out(shifter_2_out));
  Shifter #(.width(32), .shift("ar")) shifter_3 (
    .in({inst[31], inst[7], inst[30:25], inst[11:8], {20{1'b0}}}), .\dist (5'b10011), .out(shifter_3_out));
  Shifter #(.width(32), .shift("ar")) shifter_4 (
    .in({inst[31], inst[19:12], inst[20], inst[30:21], {12{1'b0}}}), .\dist (5'b01011), .out(shifter_4_out));
  Multiplexer #(.select(3), .width(32), .enable("false")) multiplexer_1 (
    .in1(shifter_1_out), .in2(shifter_2_out), .in3(shifter_3_out), .in4({inst[31:12], {12{1'b0}}}),
    .in5(shifter_4_out), .out(imm), .sel(ImmSel));  // open: in0, in6, in7

  // Notes on the sheet:
  //   INPUTS to your circuit
  //   DON'T CHANGE THE LOCATIONS OF THE INPUTS AND OUTPUTS!
  //   OUTPUT from your circuit
endmodule
