// Logisim project regfile.circ as structural Verilog: 1 circuit, main circuit main
module main (
  input  [4:0] rs1,
  input  [4:0] rs2,
  input  [4:0] rd,
  input  [31:0] Write_Data,
  input  RegWEn,
  input  clk,
  output [31:0] ra,
  output [31:0] sp,
  output [31:0] t0,
  output [31:0] t1,
  output [31:0] t2,
  output [31:0] s0,
  output [31:0] s1,
  output [31:0] a0,
  output [31:0] Read_Data_1,
  output [31:0] Read_Data_2
);

  wire a0_en, ra_en, s0_en, s1_en, sp_en, t0_en, t1_en, t2_en;
  wire [31:0] a0in, ra1, s0in, s1in, sp1, t0in, t1in, t2in, x0;

  Demultiplexer #(.select(5), .enable("false")) demultiplexer_1 (
    .out1(ra_en), .out2(sp_en), .out5(t0_en), .out6(t1_en), .out7(t2_en), .out8(s0_en), .out9(s1_en),
    .out10(a0_en), .in(RegWEn), .sel(rd));  // open: out0, out3, out4, out11, out12, out13, out14, out15, out16, out17, out18, out19, out20, out21, out22, out23, out24, out25, out26, out27, out28, out29, out30, out31
  Demultiplexer #(.select(5), .width(32), .enable("false")) demultiplexer_2 (
    .out1(ra1), .out2(sp1), .out5(t0in), .out6(t1in), .out7(t2in), .out8(s0in), .out9(s1in), .out10(a0in),
    .in(Write_Data), .sel(rd));  // open: out0, out3, out4, out11, out12, out13, out14, out15, out16, out17, out18, out19, out20, out21, out22, out23, out24, out25, out26, out27, out28, out29, out30, out31
  Register #(.width(32)) register_1 (.D(s0in), .en(s0_en), .clk(clk), .Q(s0));  // open: clr
  Register #(.width(32)) register_2 (.D(s1in), .en(s1_en), .clk(clk), .Q(s1));  // open: clr
  Register #(.width(32)) register_3 (.D({32{1'b0}}), .clk(clk), .Q(x0));  // open: en, clr
  Register #(.width(32)) register_4 (.D(ra1), .en(ra_en), .clk(clk), .Q(ra));  // open: clr
  Register #(.width(32)) register_5 (.D(sp1), .en(sp_en), .clk(clk), .Q(sp));  // open: clr
  Register #(.width(32)) register_6 (.D(t0in), .en(t0_en), .clk(clk), .Q(t0));  // open: clr
  Register #(.width(32)) register_7 (.D(t1in), .en(t1_en), .clk(clk), .Q(t1));  // open: clr
  Register #(.width(32)) register_8 (.D(t2in), .en(t2_en), .clk(clk), .Q(t2));  // open: clr
  Register #(.width(32)) register_9 (.D(a0in), .en(a0_en), .clk(clk), .Q(a0));  // open: clr
  Multiplexer #(.select(5), .width(32), .enable("false")) multiplexer_1 (
    .in0(x0), .in1(ra), .in2(sp), .in5(t0), .in6(t1), .in7(t2), .in8(s0), .in9(s1), .in10(a0),
    .out(Read_Data_1), .sel(rs1));  // open: in3, in4, in11, in12, in13, in14, in15, in16, in17, in18, in19, in20, in21, in22, in23, in24, in25, in26, in27, in28, in29, in30, in31
  Multiplexer #(.select(5), .width(32), .enable("false")) multiplexer_2 (
    .in0(x0), .in1(ra), .in2(sp), .in5(t0), .in6(t1), .in7(t2), .in8(s0), .in9(s1), .in10(a0),
    .out(Read_Data_2), .sel(rs2));  // open: in3, in4, in11, in12, in13, in14, in15, in16, in17, in18, in19, in20, in21, in22, in23, in24, in25, in26, in27, in28, in29, in30, in31

  // Other names for the same wires on the sheet: read_data1[31:0] = Read_Data_1; read_data2[31:0] = Read_Data_2;
  //   read_reg1[4:0] = rs1; read_reg2[4:0] = rs2; write_en = RegWEn; write_reg[4:0] = rd

  // Notes on the sheet:
  //   INPUTS to your circuit
  //   DON'T CHANGE THE LOCATIONS OF THE INPUTS AND OUTPUTS!
  //   These are DEBUG/TEST outputs from your circuit.
  //   OUTPUTS from your circuit
endmodule
